// Logisim project Halbaddierer Jonas Roth.circ as structural Verilog
module Halbaddierer (
  input  in_1,
  input  in_2
);

  wire and_1_out, xor_1_out;

  and and_1 (and_1_out, in_1, in_2);
  xor xor_1 (xor_1_out, in_2, in_1);
  LED led_1 (.in(and_1_out));
  LED led_2 (.in(xor_1_out));
endmodule
