// Logisim project Werner.circ as structural Verilog: 15 circuits, main circuit main
module main (
);

  wire button_1_out, button_2_out, button_3_out, button_4_out, t_ff_21_q;
  wire [3:0] n8bit_dffr_1_output, n8bit_dffr_1_output_2, n8bit_dffr_2_output, n8bit_dffr_2_output_2,
       t_ff_1_q, t_ff_5_q, t_ff_17_q;
  wire [7:0] bit_extender_1_out, bit_extender_2_out, bit_extender_3_out, n16byte_sram_1_out_6, t_ff_9_q;
  wire [8:0] n8bit_subtractor_1_out_3;

  T_Flip_Flop t_ff_1 (.Q(t_ff_1_q[0]));  // open: clk, T, Qn, preset, reset, en
  T_Flip_Flop t_ff_2 (.Q(t_ff_1_q[1]));  // open: clk, T, Qn, preset, reset, en
  T_Flip_Flop t_ff_3 (.Q(t_ff_1_q[2]));  // open: clk, T, Qn, preset, reset, en
  T_Flip_Flop t_ff_4 (.Q(t_ff_1_q[3]));  // open: clk, T, Qn, preset, reset, en
  T_Flip_Flop t_ff_5 (.Q(t_ff_5_q[0]));  // open: clk, T, Qn, preset, reset, en
  T_Flip_Flop t_ff_6 (.Q(t_ff_5_q[1]));  // open: clk, T, Qn, preset, reset, en
  T_Flip_Flop t_ff_7 (.Q(t_ff_5_q[2]));  // open: clk, T, Qn, preset, reset, en
  T_Flip_Flop t_ff_8 (.Q(t_ff_5_q[3]));  // open: clk, T, Qn, preset, reset, en
  assign bit_extender_1_out = {{4{1'b0}}, t_ff_1_q};  // Bit_Extender bit_extender_1
  assign bit_extender_2_out = {{4{1'b0}}, t_ff_5_q};  // Bit_Extender bit_extender_2
  T_Flip_Flop t_ff_9 (.Q(t_ff_9_q[0]));  // open: clk, T, Qn, preset, reset, en
  T_Flip_Flop t_ff_10 (.Q(t_ff_9_q[1]));  // open: clk, T, Qn, preset, reset, en
  T_Flip_Flop t_ff_11 (.Q(t_ff_9_q[2]));  // open: clk, T, Qn, preset, reset, en
  T_Flip_Flop t_ff_12 (.Q(t_ff_9_q[3]));  // open: clk, T, Qn, preset, reset, en
  T_Flip_Flop t_ff_13 (.Q(t_ff_9_q[4]));  // open: clk, T, Qn, preset, reset, en
  T_Flip_Flop t_ff_14 (.Q(t_ff_9_q[5]));  // open: clk, T, Qn, preset, reset, en
  T_Flip_Flop t_ff_15 (.Q(t_ff_9_q[6]));  // open: clk, T, Qn, preset, reset, en
  T_Flip_Flop t_ff_16 (.Q(t_ff_9_q[7]));  // open: clk, T, Qn, preset, reset, en
  Hex_Digit_Display hex_digit_display_1 (.value(n8bit_dffr_2_output_2));  // open: dp
  Hex_Digit_Display hex_digit_display_2 (.value(n8bit_dffr_2_output));  // open: dp
  _8bit_Subtractor u_8bit_subtractor_1 (
    .A(bit_extender_1_out), .B(bit_extender_2_out), .out_3(n8bit_subtractor_1_out_3));
  T_Flip_Flop t_ff_17 (.Q(t_ff_17_q[0]));  // open: clk, T, Qn, preset, reset, en
  T_Flip_Flop t_ff_18 (.Q(t_ff_17_q[1]));  // open: clk, T, Qn, preset, reset, en
  T_Flip_Flop t_ff_19 (.Q(t_ff_17_q[2]));  // open: clk, T, Qn, preset, reset, en
  T_Flip_Flop t_ff_20 (.Q(t_ff_17_q[3]));  // open: clk, T, Qn, preset, reset, en
  Hex_Digit_Display hex_digit_display_3 (.value(n8bit_dffr_1_output));  // open: dp
  Hex_Digit_Display hex_digit_display_4 (.value(n8bit_dffr_1_output_2));  // open: dp
  assign bit_extender_3_out = {{7{1'b0}}, n8bit_subtractor_1_out_3[8]};  // Bit_Extender bit_extender_3
  Button button_1 (.out(button_1_out));
  Button button_2 (.out(button_2_out));
  Button button_3 (.out(button_3_out));
  Button button_4 (.out(button_4_out));
  T_Flip_Flop t_ff_21 (.Q(t_ff_21_q));  // open: clk, T, Qn, preset, reset, en
  _8bit_DFFR u_8bit_dffr_1 (
    .Input(n8bit_subtractor_1_out_3[7:0]), .Clock(button_1_out), .Reset(button_2_out),
    .Output({n8bit_dffr_1_output_2, n8bit_dffr_1_output}));
  _8bit_DFFR u_8bit_dffr_2 (
    .Input(bit_extender_3_out), .Clock(button_1_out), .Reset(button_2_out),
    .Output({n8bit_dffr_2_output_2, n8bit_dffr_2_output}));
  _16byte_SRAM u_16byte_sram_1 (
    .Data(t_ff_9_q), .Adress(t_ff_17_q), .Write(button_3_out), .Read(t_ff_21_q), .Reset(button_4_out),
    .out_6(n16byte_sram_1_out_6));
  Hex_Digit_Display hex_digit_display_5 (.value(n16byte_sram_1_out_6[7:4]));  // open: dp
  Hex_Digit_Display hex_digit_display_6 (.value(n16byte_sram_1_out_6[3:0]));  // open: dp
endmodule

module Half_Adder (
  input  in_1,
  input  in_2,
  output out_3,
  output out_4
);

  xor xor_1 (out_3, in_1, in_2);
  and and_1 (out_4, in_2, in_1);
endmodule

module Full_Adder (
  input  in_1,
  input  in_2,
  input  in_3,
  output out_4,
  output out_5
);

  wire half_adder_1_out_3, half_adder_1_out_4, half_adder_2_out_4;

  Half_Adder half_adder_1 (.in_1(in_2), .in_2(in_3), .out_3(half_adder_1_out_3), .out_4(half_adder_1_out_4));
  Half_Adder half_adder_2 (.in_1(half_adder_1_out_3), .in_2(in_1), .out_3(out_4), .out_4(half_adder_2_out_4));
  or or_1 (out_5, half_adder_2_out_4, half_adder_1_out_4);
endmodule

module _4bit_Adder (
  input  C_in,
  input  A0,
  input  A1,
  input  A2,
  input  A3,
  input  B0,
  input  B1,
  input  B2,
  input  B3,
  output S0,
  output S1,
  output S2,
  output S3,
  output C_out
);

  wire full_adder_1_out_5, full_adder_2_out_5, full_adder_3_out_5;

  Full_Adder full_adder_1 (.in_1(C_in), .in_2(A0), .in_3(B0), .out_4(S0), .out_5(full_adder_1_out_5));
  Full_Adder full_adder_2 (.in_1(full_adder_1_out_5), .in_2(A1), .in_3(B1), .out_4(S1), .out_5(full_adder_2_out_5));
  Full_Adder full_adder_3 (.in_1(full_adder_2_out_5), .in_2(A2), .in_3(B2), .out_4(S2), .out_5(full_adder_3_out_5));
  Full_Adder full_adder_4 (.in_1(full_adder_3_out_5), .in_2(A3), .in_3(B3), .out_4(S3), .out_5(C_out));
endmodule

module _8bit_Adder (
  input  [7:0] A,
  input  [7:0] B,
  output [8:0] out_3
);

  wire n4bit_adder_1_c_out;

  _4bit_Adder u_4bit_adder_1 (
    .A0(A[0]), .A1(A[1]), .A2(A[2]), .A3(A[3]), .B0(B[0]), .B1(B[1]), .B2(B[2]), .B3(B[3]), .S0(out_3[0]),
    .S1(out_3[1]), .S2(out_3[2]), .S3(out_3[3]), .C_out(n4bit_adder_1_c_out), .C_in(1'b0));
  _4bit_Adder u_4bit_adder_2 (
    .A0(A[4]), .A1(A[5]), .A2(A[6]), .A3(A[7]), .B0(B[4]), .B1(B[5]), .B2(B[6]), .B3(B[7]), .S0(out_3[4]),
    .S1(out_3[5]), .S2(out_3[6]), .S3(out_3[7]), .C_out(out_3[8]), .C_in(n4bit_adder_1_c_out));
endmodule

module _8bit_DFFR (
  input  [7:0] Input,
  input  Clock,
  input  Reset,
  output [7:0] Output
);

  DFFR dffr_1 (.Set(Input[0]), .Clock(Clock), .Reset(Reset), .out_4(Output[0]));  // open: out_5
  DFFR dffr_2 (.Set(Input[1]), .Clock(Clock), .Reset(Reset), .out_4(Output[1]));  // open: out_5
  DFFR dffr_3 (.Set(Input[2]), .Clock(Clock), .Reset(Reset), .out_4(Output[2]));  // open: out_5
  DFFR dffr_4 (.Set(Input[3]), .Clock(Clock), .Reset(Reset), .out_4(Output[3]));  // open: out_5
  DFFR dffr_5 (.Set(Input[4]), .Clock(Clock), .Reset(Reset), .out_4(Output[4]));  // open: out_5
  DFFR dffr_6 (.Set(Input[5]), .Clock(Clock), .Reset(Reset), .out_4(Output[5]));  // open: out_5
  DFFR dffr_7 (.Set(Input[6]), .Clock(Clock), .Reset(Reset), .out_4(Output[6]));  // open: out_5
  DFFR dffr_8 (.Set(Input[7]), .Clock(Clock), .Reset(Reset), .out_4(Output[7]));  // open: out_5
endmodule

module DFFR (
  input  Set,
  input  Clock,
  input  Reset,
  output out_4,
  output out_5
);

  wire not_1_out;

  not not_1 (not_1_out, Set);
  S_R_Flip_Flop s_r_ff_1 (
    .S(Set), .clk(Clock), .R(not_1_out), .Q(out_4), .Qn(out_5), .reset(Reset));  // open: preset, en
endmodule

module _8bit_SRAM (
  input  [7:0] D,
  input  Write,
  input  Read,
  input  Reset,
  output [7:0] Output
);

  wire [7:0] n8bit_dffr_1_output;

  _8bit_DFFR u_8bit_dffr_1 (.Input(D), .Clock(Write), .Reset(Reset), .Output(n8bit_dffr_1_output));
  _8_1_AND u_8_1_and_1 (.A(n8bit_dffr_1_output), .B(Read), .out_3(Output));
endmodule

module _8_1_AND (
  input  [7:0] A,
  input  B,
  output [7:0] out_3
);

  and and_1 (out_3[0], A[0], B);
  and and_2 (out_3[1], A[1], B);
  and and_3 (out_3[2], A[2], B);
  and and_4 (out_3[3], A[3], B);
  and and_5 (out_3[4], A[4], B);
  and and_6 (out_3[5], A[5], B);
  and and_7 (out_3[6], A[6], B);
  and and_8 (out_3[7], A[7], B);
endmodule

module _16byte_SRAM (
  input  [7:0] Data,
  input  [3:0] Adress,
  input  Write,
  input  Read,
  input  Reset,
  output [7:0] out_6
);

  wire decoder_1_out0, decoder_1_out1, decoder_1_out2, decoder_1_out3, decoder_1_out4, decoder_1_out5,
       decoder_1_out6, decoder_1_out7, decoder_1_out8, decoder_1_out9, decoder_1_out10, decoder_1_out11,
       decoder_1_out12, decoder_1_out13, decoder_1_out14, decoder_1_out15, sram_and_1_read_out,
       sram_and_1_reset_out, sram_and_1_write_out, sram_and_2_read_out, sram_and_2_reset_out,
       sram_and_2_write_out, sram_and_3_read_out, sram_and_3_reset_out, sram_and_3_write_out,
       sram_and_4_read_out, sram_and_4_reset_out, sram_and_4_write_out, sram_and_5_read_out,
       sram_and_5_reset_out, sram_and_5_write_out, sram_and_6_read_out, sram_and_6_reset_out,
       sram_and_6_write_out, sram_and_7_read_out, sram_and_7_reset_out, sram_and_7_write_out,
       sram_and_8_read_out, sram_and_8_reset_out, sram_and_8_write_out, sram_and_9_read_out,
       sram_and_9_reset_out, sram_and_9_write_out, sram_and_10_read_out, sram_and_10_reset_out,
       sram_and_10_write_out, sram_and_11_read_out, sram_and_11_reset_out, sram_and_11_write_out,
       sram_and_12_read_out, sram_and_12_reset_out, sram_and_12_write_out, sram_and_13_read_out,
       sram_and_13_reset_out, sram_and_13_write_out, sram_and_14_read_out, sram_and_14_reset_out,
       sram_and_14_write_out, sram_and_15_read_out, sram_and_15_reset_out, sram_and_15_write_out,
       sram_and_16_read_out, sram_and_16_reset_out, sram_and_16_write_out;
  wire [7:0] n8bit_sram_1_output, n8bit_sram_2_output, n8bit_sram_3_output, n8bit_sram_4_output,
       n8bit_sram_5_output, n8bit_sram_6_output, n8bit_sram_7_output, n8bit_sram_8_output,
       n8bit_sram_9_output, n8bit_sram_10_output, n8bit_sram_11_output, n8bit_sram_12_output,
       n8bit_sram_13_output, n8bit_sram_14_output, n8bit_sram_15_output, n8bit_sram_16_output;

  SRAM_AND sram_and_1 (
    .Select(decoder_1_out0), .Write_in(Write), .Read_in(Read), .Reset_in(Reset),
    .Write_out(sram_and_1_write_out), .Read_out(sram_and_1_read_out), .Reset_out(sram_and_1_reset_out));
  SRAM_AND sram_and_2 (
    .Select(decoder_1_out1), .Write_in(Write), .Read_in(Read), .Reset_in(Reset),
    .Write_out(sram_and_2_write_out), .Read_out(sram_and_2_read_out), .Reset_out(sram_and_2_reset_out));
  SRAM_AND sram_and_3 (
    .Select(decoder_1_out2), .Write_in(Write), .Read_in(Read), .Reset_in(Reset),
    .Write_out(sram_and_3_write_out), .Read_out(sram_and_3_read_out), .Reset_out(sram_and_3_reset_out));
  SRAM_AND sram_and_4 (
    .Select(decoder_1_out3), .Write_in(Write), .Read_in(Read), .Reset_in(Reset),
    .Write_out(sram_and_4_write_out), .Read_out(sram_and_4_read_out), .Reset_out(sram_and_4_reset_out));
  SRAM_AND sram_and_5 (
    .Select(decoder_1_out4), .Write_in(Write), .Read_in(Read), .Reset_in(Reset),
    .Write_out(sram_and_5_write_out), .Read_out(sram_and_5_read_out), .Reset_out(sram_and_5_reset_out));
  SRAM_AND sram_and_6 (
    .Select(decoder_1_out5), .Write_in(Write), .Read_in(Read), .Reset_in(Reset),
    .Write_out(sram_and_6_write_out), .Read_out(sram_and_6_read_out), .Reset_out(sram_and_6_reset_out));
  SRAM_AND sram_and_7 (
    .Select(decoder_1_out6), .Write_in(Write), .Read_in(Read), .Reset_in(Reset),
    .Write_out(sram_and_7_write_out), .Read_out(sram_and_7_read_out), .Reset_out(sram_and_7_reset_out));
  SRAM_AND sram_and_8 (
    .Select(decoder_1_out7), .Write_in(Write), .Read_in(Read), .Reset_in(Reset),
    .Write_out(sram_and_8_write_out), .Read_out(sram_and_8_read_out), .Reset_out(sram_and_8_reset_out));
  _8bit_SRAM u_8bit_sram_1 (
    .D(Data), .Write(sram_and_1_write_out), .Read(sram_and_1_read_out), .Output(n8bit_sram_1_output),
    .Reset(sram_and_1_reset_out));
  _8bit_SRAM u_8bit_sram_2 (
    .D(Data), .Write(sram_and_2_write_out), .Read(sram_and_2_read_out), .Output(n8bit_sram_2_output),
    .Reset(sram_and_2_reset_out));
  _8bit_SRAM u_8bit_sram_3 (
    .D(Data), .Write(sram_and_3_write_out), .Read(sram_and_3_read_out), .Output(n8bit_sram_3_output),
    .Reset(sram_and_3_reset_out));
  _8bit_SRAM u_8bit_sram_4 (
    .D(Data), .Write(sram_and_4_write_out), .Read(sram_and_4_read_out), .Output(n8bit_sram_4_output),
    .Reset(sram_and_4_reset_out));
  _8bit_SRAM u_8bit_sram_5 (
    .D(Data), .Write(sram_and_5_write_out), .Read(sram_and_5_read_out), .Output(n8bit_sram_5_output),
    .Reset(sram_and_5_reset_out));
  _8bit_SRAM u_8bit_sram_6 (
    .D(Data), .Write(sram_and_6_write_out), .Read(sram_and_6_read_out), .Output(n8bit_sram_6_output),
    .Reset(sram_and_6_reset_out));
  _8bit_SRAM u_8bit_sram_7 (
    .D(Data), .Write(sram_and_7_write_out), .Read(sram_and_7_read_out), .Output(n8bit_sram_7_output),
    .Reset(sram_and_7_reset_out));
  _8bit_SRAM u_8bit_sram_8 (
    .D(Data), .Write(sram_and_8_write_out), .Read(sram_and_8_read_out), .Output(n8bit_sram_8_output),
    .Reset(sram_and_8_reset_out));
  Decoder #(.select(4)) decoder_1 (
    .out0(decoder_1_out0), .out1(decoder_1_out1), .out2(decoder_1_out2), .out3(decoder_1_out3),
    .out4(decoder_1_out4), .out5(decoder_1_out5), .out6(decoder_1_out6), .out7(decoder_1_out7),
    .out8(decoder_1_out8), .out9(decoder_1_out9), .out10(decoder_1_out10), .out11(decoder_1_out11),
    .out12(decoder_1_out12), .out13(decoder_1_out13), .out14(decoder_1_out14), .out15(decoder_1_out15),
    .sel(Adress));  // open: en
  assign out_6 = n8bit_sram_8_output | n8bit_sram_7_output | n8bit_sram_6_output | n8bit_sram_5_output | n8bit_sram_4_output | n8bit_sram_3_output | n8bit_sram_2_output | n8bit_sram_1_output | n8bit_sram_9_output | n8bit_sram_10_output | n8bit_sram_11_output | n8bit_sram_12_output | n8bit_sram_13_output | n8bit_sram_14_output | n8bit_sram_15_output | n8bit_sram_16_output;  // OR_Gate or_1, 8 bits wide
  _8bit_SRAM u_8bit_sram_9 (
    .D(Data), .Write(sram_and_9_write_out), .Read(sram_and_9_read_out), .Output(n8bit_sram_9_output),
    .Reset(sram_and_9_reset_out));
  _8bit_SRAM u_8bit_sram_10 (
    .D(Data), .Write(sram_and_10_write_out), .Read(sram_and_10_read_out), .Output(n8bit_sram_10_output),
    .Reset(sram_and_10_reset_out));
  _8bit_SRAM u_8bit_sram_11 (
    .D(Data), .Write(sram_and_11_write_out), .Read(sram_and_11_read_out), .Output(n8bit_sram_11_output),
    .Reset(sram_and_11_reset_out));
  _8bit_SRAM u_8bit_sram_12 (
    .D(Data), .Write(sram_and_12_write_out), .Read(sram_and_12_read_out), .Output(n8bit_sram_12_output),
    .Reset(sram_and_12_reset_out));
  _8bit_SRAM u_8bit_sram_13 (
    .D(Data), .Write(sram_and_13_write_out), .Read(sram_and_13_read_out), .Output(n8bit_sram_13_output),
    .Reset(sram_and_13_reset_out));
  _8bit_SRAM u_8bit_sram_14 (
    .D(Data), .Write(sram_and_14_write_out), .Read(sram_and_14_read_out), .Output(n8bit_sram_14_output),
    .Reset(sram_and_14_reset_out));
  _8bit_SRAM u_8bit_sram_15 (
    .D(Data), .Write(sram_and_15_write_out), .Read(sram_and_15_read_out), .Output(n8bit_sram_15_output),
    .Reset(sram_and_15_reset_out));
  _8bit_SRAM u_8bit_sram_16 (
    .D(Data), .Write(sram_and_16_write_out), .Read(sram_and_16_read_out), .Output(n8bit_sram_16_output),
    .Reset(sram_and_16_reset_out));
  SRAM_AND sram_and_9 (
    .Select(decoder_1_out15), .Write_in(Write), .Read_in(Read), .Reset_in(Reset),
    .Write_out(sram_and_9_write_out), .Read_out(sram_and_9_read_out), .Reset_out(sram_and_9_reset_out));
  SRAM_AND sram_and_10 (
    .Select(decoder_1_out14), .Write_in(Write), .Read_in(Read), .Reset_in(Reset),
    .Write_out(sram_and_10_write_out), .Read_out(sram_and_10_read_out), .Reset_out(sram_and_10_reset_out));
  SRAM_AND sram_and_11 (
    .Select(decoder_1_out13), .Write_in(Write), .Read_in(Read), .Reset_in(Reset),
    .Write_out(sram_and_11_write_out), .Read_out(sram_and_11_read_out), .Reset_out(sram_and_11_reset_out));
  SRAM_AND sram_and_12 (
    .Select(decoder_1_out12), .Write_in(Write), .Read_in(Read), .Reset_in(Reset),
    .Write_out(sram_and_12_write_out), .Read_out(sram_and_12_read_out), .Reset_out(sram_and_12_reset_out));
  SRAM_AND sram_and_13 (
    .Select(decoder_1_out11), .Write_in(Write), .Read_in(Read), .Reset_in(Reset),
    .Write_out(sram_and_13_write_out), .Read_out(sram_and_13_read_out), .Reset_out(sram_and_13_reset_out));
  SRAM_AND sram_and_14 (
    .Select(decoder_1_out10), .Write_in(Write), .Read_in(Read), .Reset_in(Reset),
    .Write_out(sram_and_14_write_out), .Read_out(sram_and_14_read_out), .Reset_out(sram_and_14_reset_out));
  SRAM_AND sram_and_15 (
    .Select(decoder_1_out9), .Write_in(Write), .Read_in(Read), .Reset_in(Reset),
    .Write_out(sram_and_15_write_out), .Read_out(sram_and_15_read_out), .Reset_out(sram_and_15_reset_out));
  SRAM_AND sram_and_16 (
    .Select(decoder_1_out8), .Write_in(Write), .Read_in(Read), .Reset_in(Reset),
    .Write_out(sram_and_16_write_out), .Read_out(sram_and_16_read_out), .Reset_out(sram_and_16_reset_out));
endmodule

module SRAM_AND (
  input  Select,
  input  Write_in,
  input  Read_in,
  input  Reset_in,
  output Write_out,
  output Read_out,
  output Reset_out
);

  and and_1 (Write_out, Select, Write_in);
  and and_2 (Read_out, Select, Read_in);
  and and_3 (Reset_out, Select, Reset_in);
endmodule

module _256_byte_SRAM (
);

  wire [7:0] n16byte_sram_1_out_6, n16byte_sram_2_out_6, n16byte_sram_3_out_6, n16byte_sram_4_out_6,
       n16byte_sram_5_out_6, n16byte_sram_6_out_6, n16byte_sram_7_out_6, n16byte_sram_8_out_6,
       n16byte_sram_9_out_6, n16byte_sram_10_out_6, n16byte_sram_11_out_6, n16byte_sram_12_out_6,
       n16byte_sram_13_out_6, n16byte_sram_14_out_6, n16byte_sram_15_out_6, n16byte_sram_16_out_6;

  _16byte_SRAM u_16byte_sram_1 (.out_6(n16byte_sram_1_out_6));  // open: Data, Adress, Write, Read, Reset
  _16byte_SRAM u_16byte_sram_2 (.out_6(n16byte_sram_2_out_6));  // open: Data, Adress, Write, Read, Reset
  _16byte_SRAM u_16byte_sram_3 (.out_6(n16byte_sram_3_out_6));  // open: Data, Adress, Write, Read, Reset
  _16byte_SRAM u_16byte_sram_4 (.out_6(n16byte_sram_4_out_6));  // open: Data, Adress, Write, Read, Reset
  _16byte_SRAM u_16byte_sram_5 (.out_6(n16byte_sram_5_out_6));  // open: Data, Adress, Write, Read, Reset
  _16byte_SRAM u_16byte_sram_6 (.out_6(n16byte_sram_6_out_6));  // open: Data, Adress, Write, Read, Reset
  _16byte_SRAM u_16byte_sram_7 (.out_6(n16byte_sram_7_out_6));  // open: Data, Adress, Write, Read, Reset
  _16byte_SRAM u_16byte_sram_8 (.out_6(n16byte_sram_8_out_6));  // open: Data, Adress, Write, Read, Reset
  // OR_Gate or_1 has open pins: in0=n16byte_sram_8_out_6, in1=n16byte_sram_7_out_6, in2=n16byte_sram_6_out_6, in3=n16byte_sram_5_out_6, in4=n16byte_sram_4_out_6, in5=n16byte_sram_3_out_6, in6=n16byte_sram_2_out_6, in7=n16byte_sram_1_out_6, in8=n16byte_sram_9_out_6, in9=n16byte_sram_10_out_6, in10=n16byte_sram_11_out_6, in11=n16byte_sram_12_out_6, in12=n16byte_sram_13_out_6, in13=n16byte_sram_14_out_6, in14=n16byte_sram_15_out_6, in15=n16byte_sram_16_out_6, out=open
  _16byte_SRAM u_16byte_sram_9 (.out_6(n16byte_sram_9_out_6));  // open: Data, Adress, Write, Read, Reset
  _16byte_SRAM u_16byte_sram_10 (.out_6(n16byte_sram_10_out_6));  // open: Data, Adress, Write, Read, Reset
  _16byte_SRAM u_16byte_sram_11 (.out_6(n16byte_sram_11_out_6));  // open: Data, Adress, Write, Read, Reset
  _16byte_SRAM u_16byte_sram_12 (.out_6(n16byte_sram_12_out_6));  // open: Data, Adress, Write, Read, Reset
  _16byte_SRAM u_16byte_sram_13 (.out_6(n16byte_sram_13_out_6));  // open: Data, Adress, Write, Read, Reset
  _16byte_SRAM u_16byte_sram_14 (.out_6(n16byte_sram_14_out_6));  // open: Data, Adress, Write, Read, Reset
  _16byte_SRAM u_16byte_sram_15 (.out_6(n16byte_sram_15_out_6));  // open: Data, Adress, Write, Read, Reset
  _16byte_SRAM u_16byte_sram_16 (.out_6(n16byte_sram_16_out_6));  // open: Data, Adress, Write, Read, Reset
endmodule

module Half_Subtractor (
  input  A,
  input  B,
  output Diff,
  output Borrow
);

  wire not_1_out;

  not not_1 (not_1_out, A);
  xnor xnor_1 (Diff, A, B);
  and and_1 (Borrow, not_1_out, B);
endmodule

module Full_Subtractor (
  input  B_In,
  input  A,
  input  B,
  output Diff,
  output Borrow
);

  wire half_subtractor_1_borrow, half_subtractor_1_diff, half_subtractor_2_borrow;

  Half_Subtractor half_subtractor_1 (.A(A), .B(B), .Diff(half_subtractor_1_diff), .Borrow(half_subtractor_1_borrow));
  Half_Subtractor half_subtractor_2 (
    .A(half_subtractor_1_diff), .B(B_In), .Diff(Diff), .Borrow(half_subtractor_2_borrow));
  or or_1 (Borrow, half_subtractor_2_borrow, half_subtractor_1_borrow);
endmodule

module _8bit_Subtractor (
  input  [7:0] A,
  input  [7:0] B,
  output [8:0] out_3
);

  wire full_subtractor_1_borrow, full_subtractor_2_borrow, full_subtractor_3_borrow,
       full_subtractor_4_borrow, full_subtractor_5_borrow, full_subtractor_6_borrow, full_subtractor_7_borrow;

  Full_Subtractor full_subtractor_1 (
    .A(A[0]), .B(B[0]), .B_In(1'b0), .Diff(out_3[0]), .Borrow(full_subtractor_1_borrow));
  Full_Subtractor full_subtractor_2 (
    .A(A[1]), .B(B[1]), .B_In(full_subtractor_1_borrow), .Diff(out_3[1]), .Borrow(full_subtractor_2_borrow));
  Full_Subtractor full_subtractor_3 (
    .A(A[2]), .B(B[2]), .B_In(full_subtractor_2_borrow), .Diff(out_3[2]), .Borrow(full_subtractor_3_borrow));
  Full_Subtractor full_subtractor_4 (
    .A(A[3]), .B(B[3]), .B_In(full_subtractor_3_borrow), .Diff(out_3[3]), .Borrow(full_subtractor_4_borrow));
  Full_Subtractor full_subtractor_5 (
    .A(A[4]), .B(B[4]), .B_In(full_subtractor_4_borrow), .Diff(out_3[4]), .Borrow(full_subtractor_5_borrow));
  Full_Subtractor full_subtractor_6 (
    .A(A[5]), .B(B[5]), .B_In(full_subtractor_5_borrow), .Diff(out_3[5]), .Borrow(full_subtractor_6_borrow));
  Full_Subtractor full_subtractor_7 (
    .A(A[6]), .B(B[6]), .B_In(full_subtractor_6_borrow), .Diff(out_3[6]), .Borrow(full_subtractor_7_borrow));
  Full_Subtractor full_subtractor_8 (
    .A(A[7]), .B(B[7]), .B_In(full_subtractor_7_borrow), .Diff(out_3[7]), .Borrow(out_3[8]));
endmodule
