// Logisim project Halb und Volladdierer.circ as structural Verilog: 2 circuits, main circuit Halbaddierer
module Halbaddierer (
  input  in_1,
  input  in_2,
  output out_3,
  output out_4
);

  and and_1 (out_4, in_1, in_2);
  xor xor_1 (out_3, in_1, in_2);
endmodule

module Volladdierer (
  input  in_1,
  input  in_2,
  input  in_3,
  output out_4,
  output out_5
);

  wire halbaddierer_1_out_3, halbaddierer_1_out_4, halbaddierer_2_out_4;

  Halbaddierer halbaddierer_1 (.out_3(halbaddierer_1_out_3), .out_4(halbaddierer_1_out_4), .in_1(in_1), .in_2(in_2));
  Halbaddierer halbaddierer_2 (.out_3(out_4), .out_4(halbaddierer_2_out_4), .in_1(halbaddierer_1_out_3), .in_2(in_3));
  Halbaddierer halbaddierer_3 (.out_3(out_5), .in_1(halbaddierer_1_out_4), .in_2(halbaddierer_2_out_4));  // open: out_4
endmodule
